# Fritzing sketch toilet_detector (saved by Fritzing 0.9.3b)
breadboards: 1

parts:
  R1 = Resistor [tolerance=±5% resistance=220 package=THT]
  R2 = Photocell (LDR) [package=THT]
  LED1 = LED - 5mm [color="Red (633nm)" package="5 mm [THT]"]
  Part1 = LED Matrix - Serial Interface - Red/Green/Blue
  Part2 = Photon
  R3 = Resistor [tolerance=±5% resistance=220 package=THT]
  PIR1 = PIR sensor

nets:
  GND: R1.Pin_0, Part1.GND, Part2.GND, R3.Pin_0, PIR1.GND
  N1: R1.Pin_1, LED1.cathode
  N2: R2.pin_0, R3.Pin_1
  N3: R2.pin_1, Part2.A5
  N4: LED1.anode, Part2.D2
  VCC: Part1.VCC, Part2.3V3
  N5: Part1.CS, Part2.D6
  N6: Part2.D3, PIR1.SIG
  N7: Part2.D4, PIR1.VDD
